# Fritzing sketch Project2 (saved by Fritzing 0.9.3b)
breadboards: 1

parts:
  VCC1 = Battery
  M1 = DC Motor
  Part1 = Arduino Uno (Rev3)
  S1 = Pushbutton [package="[THT]"]
  R1 = Resistor [tolerance=±5% resistance=10k package=THT]
  R2 = Rotary Potentiometer (Small) [maximum_resistance=100kΩ package=THT]
  IC1 = H-Bridge [package=THT]

nets:
  GND: VCC1.-, Part1.GND, R1.Pin_1, R2.leg2, IC1.GND1, IC1.GND2
  N1: VCC1.+, IC1.VCC2
  N2: M1.pin_1, IC1.2Y
  N3: M1.pin_2, IC1.1Y
  N4: Part1.A0, R2.wiper
  N5: Part1.D9_PWM, IC1.1_2EN
  N6: Part1.D13/SCK, S1.Pin_1, S1.Pin_2, R1.Pin_0
  N7: Part1.D2, IC1.2A
  N8: Part1.D3_PWM, IC1.1A
  N9: Part1.5V, S1.Pin_3, S1.Pin_4, R2.leg1
